# Fritzing sketch Controller-Schematic-Rev_A.1 (saved by Fritzing 0.9.10b)
circuit board: 9.47749cm x 5.38626cm
breadboards: 2

parts:
  EncCLK1 = MAX485 [package=dil08]
  EncDat1 = MAX485 [package=dil08]
  FUEL = DB15 VGA Connector [package=db15]
  OX = DB15 VGA Connector [package=db15]
  EncDat2 = MAX485 [package=dil08]
  EncCLK2 = MAX485 [package=dil08]
  R3 = Resistor [tolerance=±5% power=0.25 resistance=100 package=THT]
  R4 = Resistor [tolerance=±5% power=0.25 resistance=100 package=THT]
  R5 = Resistor [tolerance=±5% power=0.25 resistance=100 package=THT]
  R6 = Resistor [tolerance=±5% power=0.25 resistance=100 package=THT]
  R7 = Resistor [tolerance=±5% power=0.25 resistance=1k package=THT]
  R8 = Resistor [tolerance=±5% power=0.25 resistance=1k package=THT]
  Adjust-High_or_Low = Toggle Switch [package=THT]
  << = Pushbutton [package="[THT]"]
  >> = Pushbutton [package="[THT]"]
  R10 = Resistor [tolerance=±5% power=0.25 resistance=10k package=THT]
  R11 = Resistor [tolerance=±5% power=0.25 resistance=10k package=THT]
  R12 = Resistor [tolerance=±5% power=0.25 resistance=100 package=THT]
  R13 = Resistor [tolerance=±5% power=0.25 resistance=220 package=THT]
  R14 = Resistor [tolerance=±5% power=0.25 resistance=220 package=THT]
  R15 = Resistor [tolerance=±5% power=0.25 resistance=220 package=THT]
  R16 = Resistor [tolerance=±5% power=0.25 resistance=220 package=THT]
  R17 = Resistor [tolerance=±5% power=0.25 resistance=10k package=THT]
  R18 = Resistor [tolerance=±5% power=0.25 resistance=10k package=THT]
  Arduino_Nano = Arduino Nano (Rev3.0)
  LTC1690 = IC, DIP package, 8 pins [chip_label=Driver]  # not connected
  U1 = 74HC595 SMD [package="SO16 [SMD]"]  # not connected
  U2 = 74HC595 SMD [package="SO16 [SMD]"]  # not connected
  U3 = 74HC595 SMD [package="SO16 [SMD]"]  # not connected
  LTC1691 = IC, DIP package, 8 pins [chip_label=Driver]  # not connected

nets:
  N1: EncCLK1.RO, Arduino_Nano.D0/RX
  N2: EncCLK1.RE, R3.Pin_0
  GND: EncCLK1.GND, EncDat1.GND, FUEL.GND, OX.GND, EncDat2.GND, EncCLK2.GND, R3.Pin_1, R4.Pin_0, R10.Pin_0, R11.Pin_0, R12.Pin_0, R17.Pin_1, R18.Pin_1, Arduino_Nano.GND
  N3: EncCLK1.A, FUEL.CLK-
  N4: EncCLK1.B, FUEL.CLK+
  VCC: EncCLK1.VCC, EncDat1.VCC, FUEL.5V, OX.5V, EncDat2.VCC, EncCLK2.VCC, R5.Pin_1, R6.Pin_0, Adjust-High_or_Low.L1, <<.Pin_1, <<.Pin_2, >>.Pin_1, >>.Pin_2, Arduino_Nano.VIN
  N5: EncDat1.DE, R5.Pin_0
  N6: EncDat1.DI, Arduino_Nano.D1/TX
  N7: EncDat1.A, FUEL.DATA-
  N8: EncDat1.B, FUEL.DATA+
  N9: FUEL.H1, Arduino_Nano.A4
  N10: FUEL.H2, Arduino_Nano.A5
  N11: FUEL.H3, Arduino_Nano.A6
  N12: FUEL.CTRL, R13.Pin_1
  N13: FUEL.DIR, R15.Pin_1
  N14: FUEL.STOP, R7.Pin_0
  N15: FUEL.ADJ-L, OX.ADJ-L, <<.Pin_3, <<.Pin_4, R10.Pin_1, Arduino_Nano.D9
  N16: FUEL.ADJ-R, OX.ADJ-R, >>.Pin_3, >>.Pin_4, R11.Pin_1, Arduino_Nano.D2
  N17: FUEL.ADJ+, R17.Pin_0, Arduino_Nano.A0
  N18: OX.CLK+, EncCLK2.A
  N19: OX.CLK-, EncCLK2.B
  N20: OX.DATA+, EncDat2.A
  N21: OX.DATA-, EncDat2.B
  N22: OX.H1, Arduino_Nano.A3
  N23: OX.H2, Arduino_Nano.A2
  N24: OX.H3, Arduino_Nano.A1
  N25: OX.CTRL, R14.Pin_0
  N26: OX.DIR, R16.Pin_0
  N27: OX.STOP, R8.Pin_0
  N28: OX.ADJ+, R18.Pin_0, Arduino_Nano.A7
  N29: EncDat2.DE, R6.Pin_1
  N30: EncDat2.DI, Arduino_Nano.D11/MOSI
  N31: EncCLK2.RO, Arduino_Nano.D12/MISO
  N32: EncCLK2.RE, R4.Pin_1
  N33: R7.Pin_1, Arduino_Nano.D6
  N34: R8.Pin_1, Arduino_Nano.D7
  N35: Adjust-High_or_Low.COM, Arduino_Nano.D3
  N36: Adjust-High_or_Low.L2, R12.Pin_1
  N37: R13.Pin_0, Arduino_Nano.D10
  N38: R14.Pin_1, Arduino_Nano.D8
  N39: R15.Pin_0, Arduino_Nano.D5
  N40: R16.Pin_1, Arduino_Nano.D4

notes:
  MAX485EEPA+
  L        R
  Valve. Adj.
  MEAT Valve Control Board, Rev.: -.1
