# Fritzing sketch Controller-Schematic-Rev_B (saved by Fritzing 0.9.10b)
breadboards: 3

parts:
  FUEL = IC, DIP package, 8 pins [chip_label=LTC1690]
  OX = IC, DIP package, 8 pins [chip_label=LTC1690]
  LM1084-3_3V = Voltage Regulator - 3.3V [part_number=LM1084IT-3.3/NOPB package="TO220 [THT]"]
  C1 = Electrolytic Capacitor [capacitance=10µF voltage=16V part_number=ECA-1CM100I package="100 mil [THT, electrolytic]"]
  C2 = Tantalum Capacitor [capacitance=10µF voltage=10V package="200 mil [THT, tantalum]"]
  TPQ1 = DIP - 14 pins [chip_label=TPQ3906 package="DIP (Dual Inline) [THT]"]
  POWER_IN = Screw terminal - 2 pins [package=THT]
  Part3 = Arduino Nano 33 IOT
  R1 = Resistor [tolerance=±5% power=0.25 resistance=4.7k package=THT]
  R3 = Resistor [tolerance=±5% power=0.25 resistance=4.7k package=THT]
  FUEL_2 = DB9 Connector [package=db9]
  OX_2 = DB9 Connector [package=db9]
  << = Pushbutton [package="[THT]"]
  >> = Pushbutton [package="[THT]"]
  S1 = Toggle Switch [package=THT]
  R5 = Resistor [tolerance=±5% power=0.25 resistance=4.7k package=THT]
  TPQ2 = DIP - 14 pins [chip_label=TPQ3906 package="DIP (Dual Inline) [THT]"]
  R7 = Resistor [tolerance=±5% power=0.25 resistance=4.7k package=THT]
  R8 = Resistor [tolerance=±5% power=0.25 resistance=4.7k package=THT]
  R9 = Resistor [tolerance=±5% power=0.25 resistance=4.7k package=THT]
  R6 = Resistor [tolerance=±5% power=0.25 resistance=4.7k package=THT]
  C11 = Electrolytic Capacitor [capacitance=100nF voltage=100V part_number=UVR2A0R1MDD1TD package="100 mil [THT, electrolytic]"]
  C12 = Electrolytic Capacitor [capacitance=1µF voltage=50V part_number=50YXF1MEFCT15X11 package="100 mil [THT, electrolytic]"]
  C13 = Electrolytic Capacitor [capacitance=100nF voltage=100V part_number=UVR2A0R1MDD1TD package="100 mil [THT, electrolytic]"]
  C14 = Electrolytic Capacitor [capacitance=1µF voltage=50V part_number=50YXF1MEFCT15X11 package="100 mil [THT, electrolytic]"]
  R4 = Resistor [tolerance=±5% power=0.25 resistance=4.7k package=THT]
  R2 = Resistor [tolerance=±5% power=0.25 resistance=4.7k package=THT]
  R11 = Resistor [tolerance=±5% power=0.25 resistance=4.7k package=THT]
  R10 = Resistor [tolerance=±5% power=0.25 resistance=4.7k package=THT]
  R14 = Resistor [tolerance=±5% power=0.25 resistance=4.7k package=THT]
  R15 = Resistor [tolerance=±5% power=0.25 resistance=4.7k package=THT]
  R16 = Resistor [tolerance=±5% power=0.25 resistance=4.7k package=THT]
  LC_I2C = Screw terminal - 2 pins [package=THT]
  SELECT = female pin header, 3 pins [form="♀ (female)"]
  R17 = Resistor [tolerance=±5% power=0.25 resistance=4.7k package=THT]
  R18 = Resistor [tolerance=±5% power=0.25 resistance=4.7k package=THT]
  F_SAFE = male pin header, 2 pins [form="♂ (male)"]
  >>_2 = male pin header, 2 pins [form="♂ (male)"]
  <<_2 = male pin header, 2 pins [form="♂ (male)"]
  O_SAFE = male pin header, 2 pins [form="♂ (male)"]
  LED1 = RGB LED (com. cathode, rgb) [package="5 mm [THT]"]
  R22 = Trimmer Potentiometer [maximum_resistance=20kΩ knob_status=50% power=0.5W package=THT]
  R23 = Resistor [tolerance=±5% power=0.25 resistance=4.7k package=THT]
  R24 = Resistor [tolerance=±5% power=0.25 resistance=4.7k package=THT]

nets:
  GND: FUEL.pin1, FUEL.pin4, OX.pin1, OX.pin4, LM1084-3_3V.input_voltage, LM1084-3_3V.GND, C1.-, C1.+, C2.-, TPQ1.C1, TPQ1.C2, POWER_IN.pin1, POWER_IN.pin2, Part3.GND, Part3.VIN, Part3.D13~, R1.Pin_1, R3.Pin_1, FUEL_2.8, FUEL_2.9, OX_2.8, OX_2.9, <<.Pin_1, <<.Pin_2, >>.Pin_1, >>.Pin_2, R5.Pin_0, TPQ2.C1, TPQ2.C2, TPQ2.C3, TPQ2.C4, R7.Pin_1, R8.Pin_0, R9.Pin_0, R6.Pin_1, C11.-, C11.+, C12.-, C12.+, C13.-, C13.+, C14.-, C14.+, R4.Pin_1, R2.Pin_1, R14.Pin_1, R15.Pin_1, R16.Pin_0, R17.Pin_0, R18.Pin_0, F_SAFE.pin1, >>_2.pin2, <<_2.pin2, O_SAFE.pin1, R22.leg2
  N1: FUEL.pin2, TPQ1.B4, R1.Pin_0
  N2: FUEL.pin3, TPQ1.E1, R3.Pin_0
  N3: FUEL.pin5, FUEL_2.4
  N4: FUEL.pin6, FUEL_2.3
  N5: FUEL.pin7, FUEL_2.2
  N6: FUEL.pin8, FUEL_2.1
  N7: OX.pin2, TPQ1.B3, R4.Pin_0
  N8: OX.pin3, TPQ1.E2, R2.Pin_0
  N9: OX.pin5, OX_2.4
  N10: OX.pin6, OX_2.3
  N11: OX.pin7, OX_2.2
  N12: OX.pin8, OX_2.1
  N13: LM1084-3_3V.output_voltage, C2.+, TPQ1.C3, TPQ1.C4, S1.COM, R11.Pin_0, R10.Pin_0, SELECT.pin2, R23.Pin_0, R24.Pin_0
  N14: TPQ1.B1, Part3.D11/MOSI, Part3.+5V, R10.Pin_1
  N15: TPQ1.B2, Part3.A1, R14.Pin_0
  N16: TPQ1.E3, Part3.A2, R15.Pin_0
  N17: TPQ1.E4, Part3.D12~/MISO, R11.Pin_1
  N18: Part3.RESET, Part3.A7, LED1.blue_anode
  N19: Part3.D2, TPQ2.B2, R6.Pin_0
  N20: Part3.D3~, TPQ2.B1, R7.Pin_0
  N21: Part3.D4, S1.L1, R16.Pin_1, SELECT.pin3
  N22: Part3.D5~, TPQ2.B4, R8.Pin_1
  N23: Part3.D6~, TPQ2.B3, R9.Pin_1
  N24: Part3.D7, S1.L2, R5.Pin_1, SELECT.pin1
  N25: Part3.D8, >>.Pin_3, >>.Pin_4, >>_2.pin1, R23.Pin_1
  N26: Part3.D9~, <<.Pin_3, <<.Pin_4, <<_2.pin1, R24.Pin_1
  N27: Part3.D10~, LED1.red_anode
  N28: Part3.A6, LED1.green_anode
  N29: Part3.A5, LC_I2C.pin1
  N30: Part3.A4, LC_I2C.pin2
  N31: FUEL_2.5, TPQ2.E2, R18.Pin_1, O_SAFE.pin2
  N32: FUEL_2.6, TPQ2.E1
  N33: OX_2.5, TPQ2.E3, R17.Pin_1, F_SAFE.pin2
  N34: OX_2.6, TPQ2.E4
  N35: LED1.common_cathode, R22.wiper

custom parts:
  DIP - 14 pins: PNP Array
  Arduino Nano 33 IOT: The Arduino Nano 33 IoT is the easiest and cheapest point of entry to enhance existing devices (and creating new ones) to be part of the IoT and designing pico-network applications. Whether you are looking at building a sensor network connected to your office or home router, or if you want to create a BLE device sending data to a cellphone, the Nano 33 IoT is your one-stop-solution for many of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
