# Fritzing sketch Controller-Schematic-Rev_D (saved by Fritzing 0.9.10b)
breadboards: 4

parts:
  Part3 = Arduino Nano 33 IOT
  LM1084-3_3V1 = Voltage Regulator - 3.3V [part_number=LM1084IT-3.3/NOPB package="TO220 [THT]"]
  C1 = Electrolytic Capacitor [capacitance=10µF voltage=10V part_number=C1210C106J8NAC7800 package="100 mil [THT, electrolytic]"]
  OX = DB9 Connector [part_number="A-DF 09 A/KG-T2S" package=db9]
  FUEL = DB9 Connector [part_number="A-DF 09 A/KG-T2S" package=db9]
  FUEL_2 = IC, DIP package, 8 pins [chip_label=LTC1690]
  OX_2 = IC, DIP package, 8 pins [chip_label=LTC1690]
  EXT = IC, DIP package, 8 pins [chip_label=LTC1690]
  OX1 = DB9 Connector [part_number="A-DF 09 A/KG-T2S" package=db9]
  C2 = Tantalum Capacitor [capacitance=10µF voltage=10V part_number=CWR11HH106KB package="C 6032 [SMD, tantalum]"]
  C6 = Electrolytic Capacitor [capacitance=0.1µF voltage=16V part_number=C1206X104G4HAC7800 package="100 mil [THT, electrolytic]"]
  C8 = Electrolytic Capacitor [capacitance=0.1µF voltage=16V part_number=C1206X104G4HAC7800 package="100 mil [THT, electrolytic]"]
  C10 = Electrolytic Capacitor [capacitance=0.1µF voltage=16V part_number=C1206X104G4HAC7800 package="100 mil [THT, electrolytic]"]
  C3 = Electrolytic Capacitor [capacitance=1µF voltage=10V part_number=C0805C105J8NAC7800 package="100 mil [THT, electrolytic]"]
  C4 = Electrolytic Capacitor [capacitance=1µF voltage=10V part_number=C0805C105J8NAC7800 package="100 mil [THT, electrolytic]"]
  C7 = Electrolytic Capacitor [capacitance=1μF voltage=10V part_number=C0805C105J8NAC7800 package="100 mil [THT, electrolytic]"]
  C9 = Electrolytic Capacitor [capacitance=1µF voltage=10V part_number=C0805C105J8NAC7800 package="100 mil [THT, electrolytic]"]
  C5 = Electrolytic Capacitor [capacitance=0.1µF voltage=16V part_number=C1206X104G4HAC7800 package="100 mil [THT, electrolytic]"]
  YGURU_GRN = LED_BARGRAPH_10 [part_number=XGURUGX10D package=led_bargaph_10]
  XGURU_RED = LED_BARGRAPH_10 [part_number=XGURUGX10D package=led_bargaph_10]
  RES_ARR = IC, DIP package, 16 pins [chip_label=RES part_number=4116R-1-680LF]
  R1 = Resistor [tolerance=±5% power=0.25 resistance=68 package=THT]
  R2 = Resistor [tolerance=±5% power=0.25 resistance=150 package=THT]
  STEP_UP = QFN-24 [chip_label=IC part_number=SN74LXCH8T245RHLR package=QFN]
  STEP_DOWN = QFN-24 [chip_label=IC part_number=SN74LXCH8T245RHLR package=QFN]
  74AHC596 = 74HC595 [part_number=74AHC595 package="DIP16 [THT]"]
  74AHC595 = 74HC595 [part_number=74AHC595 package="DIP16 [THT]"]

nets:
  N1: Part3.RX, EXT.pin3
  N2: Part3.TX, STEP_DOWN.6
  N3: Part3.RESET, Part3.A7, STEP_DOWN.7
  GND: Part3.GND, Part3.D13~, LM1084-3_3V1.GND, C1.-, FUEL_2.pin3, FUEL_2.pin4, OX_2.pin4, EXT.pin4, OX1.5, C2.-, C6.-, C6.+, C8.-, C10.-, C3.-, C3.+, C4.-, C4.+, C7.-, C9.-, C5.-, C5.+, RES_ARR.pin1, RES_ARR.pin2, RES_ARR.pin3, RES_ARR.pin4, RES_ARR.pin5, RES_ARR.pin6, RES_ARR.pin7, RES_ARR.pin8, R1.Pin_0, R2.Pin_0, STEP_UP.2, STEP_UP.11, STEP_UP.12, STEP_UP.13, STEP_UP.22, STEP_DOWN.11, STEP_DOWN.12, STEP_DOWN.13, STEP_DOWN.22, 74AHC596.SH_CP, 74AHC596.OE, 74AHC595.SH_CP, 74AHC595.OE
  N4: Part3.D2, STEP_DOWN.9
  N5: Part3.D4, STEP_DOWN.5
  N6: Part3.D5~, OX_2.pin3
  N7: Part3.D8, 74AHC596.ST_CP, 74AHC595.ST_CP
  N8: Part3.D9~, STEP_UP.6
  N9: Part3.D10~, STEP_UP.5
  N10: Part3.D11/MOSI, Part3.+5V, 74AHC595.DS
  N11: Part3.D12~/MISO, STEP_DOWN.4
  N12: Part3.VIN, LM1084-3_3V1.output_voltage, FUEL_2.pin1, OX_2.pin1, EXT.pin1, C2.+, C8.+, C10.+, C7.+, C9.+, YGURU_GRN.A_A, STEP_UP.23, STEP_UP.24, STEP_DOWN.23, STEP_DOWN.24
  N13: Part3.A6, STEP_DOWN.8
  N14: Part3.A3, STEP_UP.3
  N15: Part3.A2, STEP_UP.4
  N16: Part3.A1, STEP_UP.7
  N17: Part3.A0, STEP_UP.8
  N18: Part3.3V3, YGURU_GRN.B_A
  N19: LM1084-3_3V1.input_voltage, C1.+, OX1.6, STEP_UP.1, STEP_DOWN.1, STEP_DOWN.2
  N20: OX.1, OX_2.pin8
  N21: OX.2, OX_2.pin7
  N22: OX.3, OX_2.pin6
  N23: OX.4, OX_2.pin5
  N24: OX.6, FUEL.6
  N25: OX.7, STEP_UP.16
  N26: OX.8, STEP_UP.18
  N27: OX.9, STEP_UP.20
  N28: FUEL.1, FUEL_2.pin8
  N29: FUEL.2, FUEL_2.pin7
  N30: FUEL.3, FUEL_2.pin6
  N31: FUEL.4, FUEL_2.pin5
  N32: FUEL.7, STEP_UP.17
  N33: FUEL.8, STEP_UP.19
  N34: FUEL.9, STEP_UP.21
  N35: FUEL_2.pin2, STEP_DOWN.20
  N36: OX_2.pin2, STEP_DOWN.19
  N37: EXT.pin2, STEP_DOWN.18
  N38: EXT.pin5, OX1.4
  N39: EXT.pin6, OX1.3
  N40: EXT.pin7, OX1.2
  N41: EXT.pin8, OX1.1
  N42: OX1.7, STEP_DOWN.15
  N43: OX1.8, STEP_DOWN.16
  N44: OX1.9, STEP_DOWN.17
  N45: YGURU_GRN.C_A, 74AHC595.Q7
  N46: YGURU_GRN.D_A, 74AHC595.Q6
  N47: YGURU_GRN.E_A, 74AHC595.Q5
  N48: YGURU_GRN.F_A, 74AHC595.Q4
  N49: YGURU_GRN.G_A, 74AHC595.Q3
  N50: YGURU_GRN.H_A, 74AHC595.Q2
  N51: YGURU_GRN.I_A, 74AHC595.Q1
  N52: YGURU_GRN.J_A, 74AHC595.Q0
  N53: YGURU_GRN.J_C, XGURU_RED.J_C, RES_ARR.pin16
  N54: YGURU_GRN.I_C, XGURU_RED.I_C, RES_ARR.pin15
  N55: YGURU_GRN.H_C, XGURU_RED.H_C, RES_ARR.pin14
  N56: YGURU_GRN.G_C, XGURU_RED.G_C, RES_ARR.pin13
  N57: YGURU_GRN.F_C, XGURU_RED.F_C, RES_ARR.pin12
  N58: YGURU_GRN.E_C, XGURU_RED.E_C, RES_ARR.pin11
  N59: YGURU_GRN.D_C, XGURU_RED.D_C, RES_ARR.pin10
  N60: YGURU_GRN.C_C, XGURU_RED.C_C, RES_ARR.pin9
  N61: YGURU_GRN.B_C, XGURU_RED.B_C, R1.Pin_1
  N62: YGURU_GRN.A_C, XGURU_RED.A_C, R2.Pin_1
  N63: XGURU_RED.C_A, 74AHC596.Q7
  N64: XGURU_RED.D_A, 74AHC596.Q6
  N65: XGURU_RED.E_A, 74AHC596.Q5
  N66: XGURU_RED.F_A, 74AHC596.Q4
  N67: XGURU_RED.G_A, 74AHC596.Q3
  N68: XGURU_RED.H_A, 74AHC596.Q2
  N69: XGURU_RED.I_A, 74AHC596.Q1
  N70: XGURU_RED.J_A, 74AHC596.Q0
  GND_2: 74AHC596.GND, 74AHC595.GND
  VCC: 74AHC596.MR, 74AHC596.VCC, 74AHC595.MR, 74AHC595.VCC
  N71: 74AHC596.DS, 74AHC595.Q7'

custom parts:
  Arduino Nano 33 IOT: The Arduino Nano 33 IoT is the easiest and cheapest point of entry to enhance existing devices (and creating new ones) to be part of the IoT and designing pico-network applications. Whether you are looking at building a sensor network connected to your office or home router, or if you want to create a BLE device sending data to a cellphone, the Nano 33 IoT is your one-stop-solution for many of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
