# Fritzing sketch Controller-Schematic-Rev_E (saved by Fritzing 0.9.10b)
breadboards: 3

parts:
  Part3 = Arduino Nano 33 IOT
  LM1084-3_3V1 = Voltage Regulator - 3.3V [part_number=LM1084IT-3.3/NOPB package="TO220 [THT]"]
  C2 = Tantalum Capacitor [capacitance=10µF voltage=15V part_number=CWR11HH106KB package="200 mil [THT, tantalum]"]
  C1 = Electrolytic Capacitor [capacitance=10µF voltage=10V part_number=C1210C106J8NAC7800 package="100 mil [THT, electrolytic]"]
  OX = DB9 Connector [part_number="A-DF 09 A/KG-T2S" package=db9]
  FUEL = DB9 Connector [part_number="A-DF 09 A/KG-T2S" package=db9]
  FUEL_2 = IC, DIP package, 8 pins [chip_label=LTC1690 part_number=LTC1690CN8#PBF]
  OX_2 = IC, DIP package, 8 pins [chip_label=LTC1690 part_number=LTC1690CN8#PBF]
  EXT = IC, DIP package, 8 pins [chip_label=LTC1690 part_number=LTC1690CN8#PBF]
  FUEL-ISO = SO16 [chip_label=ISO7740 part_number=ISO7740FQDWQ1 package=SO]
  OX-ISO = SO16 [chip_label=ISO7740 part_number=ISO7740FQDWQ1 package=SO]
  SER_EN = single row smd female pin header, 2 pins [form="♀ (female)"]
  EXT_2 = DB9 Connector [part_number="A-DF 09 A/KG-T2S" package=db9]
  74AHC597 = 74HC595 [part_number=SN74AHC595N package="DIP16 [THT]"]
  74AHC598 = 74HC595 [part_number=SN74AHC595N package="DIP16 [THT]"]
  XGURU_RED1 = LED_BARGRAPH_10 [part_number=XGURUGX10D package=led_bargaph_10]
  XGURU_GRN1 = LED_BARGRAPH_10 [part_number=XGURUGX10D package=led_bargaph_10]
  4116R-1-680LF = IC, DIP package, 16 pins [chip_label=4116R-1-680LF part_number=4116R-1-680LF]
  R3 = Resistor [tolerance=±5% power=0.25 resistance=150 package=THT]
  R4 = Resistor [tolerance=±5% power=0.25 resistance=68 package=THT]
  SN74LXCH8 = QFN-24 [chip_label=SN74LXCH8 part_number=SN74LXCH8T245RHLR package=QFN]
  C3 = Electrolytic Capacitor [capacitance=0.1µF voltage=16V part_number=C1206X104G4HAC7800 package="100 mil [THT, electrolytic]"]
  C4 = Electrolytic Capacitor [capacitance=1µF voltage=10V part_number=C0805C105J8NAC7800 package="100 mil [THT, electrolytic]"]
  C5 = Electrolytic Capacitor [capacitance=0.1µF voltage=16V part_number=C1206X104G4HAC7800 package="100 mil [THT, electrolytic]"]
  C6 = Electrolytic Capacitor [capacitance=1µF voltage=10V part_number=C0805C105J8NAC7800 package="100 mil [THT, electrolytic]"]
  C7 = Electrolytic Capacitor [capacitance=0.1µF voltage=16V part_number=C1206X104G4HAC7800 package="100 mil [THT, electrolytic]"]
  C8 = Electrolytic Capacitor [capacitance=1µF voltage=10V part_number=C0805C105J8NAC7800 package="100 mil [THT, electrolytic]"]
  C9 = Electrolytic Capacitor [capacitance=0.1µF voltage=16V part_number=C1206X104G4HAC7800 package="100 mil [THT, electrolytic]"]
  C10 = Electrolytic Capacitor [capacitance=1µF voltage=10V part_number=C0805C105J8NAC7800 package="100 mil [THT, electrolytic]"]
  C11 = Electrolytic Capacitor [capacitance=0.1µF voltage=16V part_number=C1206X104G4HAC7800 package="100 mil [THT, electrolytic]"]
  C12 = Electrolytic Capacitor [capacitance=1µF voltage=10V part_number=C0805C105J8NAC7800 package="100 mil [THT, electrolytic]"]
  C13 = Electrolytic Capacitor [capacitance=0.1µF voltage=16V part_number=C1206X104G4HAC7800 package="100 mil [THT, electrolytic]"]
  C14 = Electrolytic Capacitor [capacitance=1µF voltage=10V part_number=C0805C105J8NAC7800 package="100 mil [THT, electrolytic]"]
  C15 = Electrolytic Capacitor [capacitance=0.1µF voltage=16V part_number=C1206X104G4HAC7800 package="100 mil [THT, electrolytic]"]
  C16 = Electrolytic Capacitor [capacitance=1µF voltage=10V part_number=C0805C105J8NAC7800 package="100 mil [THT, electrolytic]"]
  C17 = Electrolytic Capacitor [capacitance=0.1µF voltage=16V part_number=C1206X104G4HAC7800 package="100 mil [THT, electrolytic]"]
  C18 = Electrolytic Capacitor [capacitance=1µF voltage=10V part_number=C0805C105J8NAC7800 package="100 mil [THT, electrolytic]"]
  C19 = Electrolytic Capacitor [capacitance=0.1µF voltage=16V part_number=C1206X104G4HAC7800 package="100 mil [THT, electrolytic]"]
  C20 = Electrolytic Capacitor [capacitance=1µF voltage=10V part_number=C0805C105J8NAC7800 package="100 mil [THT, electrolytic]"]
  C21 = Electrolytic Capacitor [capacitance=0.1µF voltage=16V part_number=C1206X104G4HAC7800 package="100 mil [THT, electrolytic]"]
  C22 = Electrolytic Capacitor [capacitance=1µF voltage=10V part_number=C0805C105J8NAC7800 package="100 mil [THT, electrolytic]"]
  C23 = Electrolytic Capacitor [capacitance=0.1µF voltage=16V part_number=C1206X104G4HAC7800 package="100 mil [THT, electrolytic]"]
  C24 = Electrolytic Capacitor [capacitance=1µF voltage=10V part_number=C0805C105J8NAC7800 package="100 mil [THT, electrolytic]"]
  C25 = Electrolytic Capacitor [capacitance=0.1µF voltage=16V part_number=C1206X104G4HAC7800 package="100 mil [THT, electrolytic]"]
  C26 = Electrolytic Capacitor [capacitance=1µF voltage=10V part_number=C0805C105J8NAC7800 package="100 mil [THT, electrolytic]"]

nets:
  N1: Part3.RX, EXT.pin3
  N2: Part3.TX, SN74LXCH8.5
  N3: Part3.RESET, Part3.A7, SN74LXCH8.6
  GND: Part3.GND, Part3.D13~, LM1084-3_3V1.GND, C2.-, C1.-, FUEL_2.pin3, FUEL_2.pin4, OX_2.pin4, EXT.pin4, SER_EN.pin1, EXT_2.5, 74AHC597.GND, 74AHC597.SH_CP, 74AHC597.OE, 74AHC598.GND, 74AHC598.SH_CP, 74AHC598.OE, 4116R-1-680LF.pin1, 4116R-1-680LF.pin2, 4116R-1-680LF.pin3, 4116R-1-680LF.pin4, 4116R-1-680LF.pin5, 4116R-1-680LF.pin6, 4116R-1-680LF.pin7, 4116R-1-680LF.pin8, R3.Pin_0, R4.Pin_0, SN74LXCH8.2, SN74LXCH8.11, SN74LXCH8.12, SN74LXCH8.13, SN74LXCH8.22, C3.-, C4.-, C5.-, C6.-, C7.-, C8.-, C9.-, C10.-, C11.-, C12.-, C13.-, C14.-, C17.-, C18.-
  N4: Part3.D2, SN74LXCH8.8
  N5: Part3.D3~, SER_EN.pin2
  N6: Part3.D4, SN74LXCH8.4
  N7: Part3.D5~, OX_2.pin3
  N8: Part3.D8, 74AHC598.ST_CP
  N9: Part3.D9~, OX-ISO.4
  N10: Part3.D10~, FUEL-ISO.4
  N11: Part3.D11/MOSI, Part3.+5V, 74AHC598.DS
  N12: Part3.D12~/MISO, SN74LXCH8.3
  N13: Part3.VIN, LM1084-3_3V1.output_voltage, C2.+, FUEL-ISO.1, OX-ISO.1, SN74LXCH8.1, C3.+, C4.+, C7.+, C8.+, C15.+, C16.+, C17.+, C18.+, C21.+, C22.+, C25.+, C26.+
  N14: Part3.A6, SN74LXCH8.7
  N15: Part3.A3, FUEL-ISO.3
  N16: Part3.A2, OX-ISO.3
  N17: Part3.A1, FUEL-ISO.5
  N18: Part3.A0, OX-ISO.5
  N19: Part3.3V3, XGURU_GRN1.B_A
  N20: LM1084-3_3V1.input_voltage, C1.+, FUEL_2.pin1, OX_2.pin1, EXT.pin1, EXT_2.6, XGURU_GRN1.A_A, SN74LXCH8.23, SN74LXCH8.24, C5.+, C6.+, C9.+, C10.+, C11.+, C12.+, C13.+, C14.+
  N21: OX.1, OX_2.pin8
  N22: OX.2, OX_2.pin7
  N23: OX.3, OX_2.pin6
  N24: OX.4, OX_2.pin5
  N25: OX.5, OX-ISO.10, OX-ISO.16, C23.+, C24.+
  N26: OX.6, OX-ISO.9, OX-ISO.15, C23.-, C24.-
  N27: OX.7, OX-ISO.14
  N28: OX.8, OX-ISO.13
  N29: OX.9, OX-ISO.12
  N30: FUEL.1, FUEL_2.pin8
  N31: FUEL.2, FUEL_2.pin7
  N32: FUEL.3, FUEL_2.pin6
  N33: FUEL.4, FUEL_2.pin5
  N34: FUEL.5, FUEL-ISO.10, FUEL-ISO.16, C19.+, C20.+
  N35: FUEL.6, FUEL-ISO.9, FUEL-ISO.15, C19.-, C20.-
  N36: FUEL.7, FUEL-ISO.14
  N37: FUEL.8, FUEL-ISO.13
  N38: FUEL.9, FUEL-ISO.12
  N39: FUEL_2.pin2, SN74LXCH8.21
  N40: OX_2.pin2, SN74LXCH8.20
  N41: EXT.pin2, SN74LXCH8.19
  N42: EXT.pin5, EXT_2.4
  N43: EXT.pin6, EXT_2.3
  N44: EXT.pin7, EXT_2.2
  N45: EXT.pin8, EXT_2.1
  N46: FUEL-ISO.2, FUEL-ISO.8, OX-ISO.2, OX-ISO.8, C15.-, C16.-, C21.-, C22.-, C25.-, C26.-
  N47: EXT_2.7, SN74LXCH8.16
  N48: EXT_2.8, SN74LXCH8.17
  N49: EXT_2.9, SN74LXCH8.18
  N50: 74AHC597.Q1, XGURU_RED1.I_A
  N51: 74AHC597.Q2, XGURU_RED1.H_A
  N52: 74AHC597.Q3, XGURU_RED1.G_A
  N53: 74AHC597.Q4, XGURU_RED1.F_A
  N54: 74AHC597.Q5, XGURU_RED1.E_A
  N55: 74AHC597.Q6, XGURU_RED1.D_A
  N56: 74AHC597.Q7, XGURU_RED1.C_A
  VCC: 74AHC597.MR, 74AHC597.VCC, 74AHC598.MR, 74AHC598.VCC
  N57: 74AHC597.DS, 74AHC598.Q7'
  N58: 74AHC597.Q0, XGURU_RED1.J_A
  N59: 74AHC598.Q1, XGURU_GRN1.I_A
  N60: 74AHC598.Q2, XGURU_GRN1.H_A
  N61: 74AHC598.Q3, XGURU_GRN1.G_A
  N62: 74AHC598.Q4, XGURU_GRN1.F_A
  N63: 74AHC598.Q5, XGURU_GRN1.E_A
  N64: 74AHC598.Q6, XGURU_GRN1.D_A
  N65: 74AHC598.Q7, XGURU_GRN1.C_A
  N66: 74AHC598.Q0, XGURU_GRN1.J_A
  N67: XGURU_RED1.J_C, XGURU_GRN1.J_C, 4116R-1-680LF.pin16
  N68: XGURU_RED1.I_C, XGURU_GRN1.I_C, 4116R-1-680LF.pin15
  N69: XGURU_RED1.H_C, XGURU_GRN1.H_C, 4116R-1-680LF.pin14
  N70: XGURU_RED1.G_C, XGURU_GRN1.G_C, 4116R-1-680LF.pin13
  N71: XGURU_RED1.F_C, XGURU_GRN1.F_C, 4116R-1-680LF.pin12
  N72: XGURU_RED1.E_C, XGURU_GRN1.E_C, 4116R-1-680LF.pin11
  N73: XGURU_RED1.D_C, XGURU_GRN1.D_C, 4116R-1-680LF.pin10
  N74: XGURU_RED1.C_C, XGURU_GRN1.C_C, 4116R-1-680LF.pin9
  N75: XGURU_RED1.B_C, XGURU_GRN1.B_C, R4.Pin_1
  N76: XGURU_RED1.A_C, XGURU_GRN1.A_C, R3.Pin_1

notes:
  Differences between Fritzing info and actual:
  >ISO 7740s are SOIC-16, not SO-16
  >Capacitor sizes (NOT what is listed in Fritzing spec):
  -CWR11HH106KB (10uF Tantalum): 2312
  -C1210C106J8NAC7800 (10uF electrolytic): 1210
  -C1206X104G4HAC7800 (.1uF): 1206
  -C0805C105J8NAC7800 (1uF): 0805
  >74HC595s are actually 74AHC595s
  >ISO7740s are SOIC-16 no SO16
  >SN74LXCH8s are VFQN-14, not QFN-24
  >XGURUX10D bar graphs are not two bar graphs, but rather 2 arrays in one 16-DIP package, with added center row for ground. There is a green array and red array, with common cathode (hence why the ground rails are connected).
  >DB9 connectors are right-angle, not out of the face of the board

custom parts:
  Arduino Nano 33 IOT: The Arduino Nano 33 IoT is the easiest and cheapest point of entry to enhance existing devices (and creating new ones) to be part of the IoT and designing pico-network applications. Whether you are looking at building a sensor network connected to your office or home router, or if you want to create a BLE device sending data to a cellphone, the Nano 33 IoT is your one-stop-solution for many of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
