# Fritzing sketch Controller-Schematic (saved by Fritzing 0.9.10b)
circuit board: 9.47749cm x 5.38626cm
breadboards: 2

parts:
  EncCLK1 = MAX485 [package=dil08]
  EncDat1 = MAX485 [package=dil08]
  Port1 = DB15 VGA Connector [package=db15]
  Port2 = DB15 VGA Connector [package=db15]
  EncDat2 = MAX485 [package=dil08]
  EncCLK2 = MAX485 [package=dil08]
  R3 = Resistor [tolerance=±5% power=0.25 resistance=100 package=THT]
  R4 = Resistor [tolerance=±5% power=0.25 resistance=100 package=THT]
  R5 = Resistor [tolerance=±5% power=0.25 resistance=100 package=THT]
  R6 = Resistor [tolerance=±5% power=0.25 resistance=100 package=THT]
  R7 = Resistor [tolerance=±5% power=0.25 resistance=1k package=THT]
  R8 = Resistor [tolerance=±5% power=0.25 resistance=1k package=THT]
  Adjust-High_or_Low = Toggle Switch [package=THT]
  << = Pushbutton [package="[THT]"]
  >> = Pushbutton [package="[THT]"]
  R10 = Resistor [tolerance=±5% power=0.25 resistance=10k package=THT]
  R11 = Resistor [tolerance=±5% power=0.25 resistance=10k package=THT]
  R12 = Resistor [tolerance=±5% power=0.25 resistance=100 package=THT]
  R13 = Resistor [tolerance=±5% power=0.25 resistance=220 package=THT]
  R14 = Resistor [tolerance=±5% power=0.25 resistance=220 package=THT]
  R15 = Resistor [tolerance=±5% power=0.25 resistance=220 package=THT]
  R16 = Resistor [tolerance=±5% power=0.25 resistance=220 package=THT]
  R17 = Resistor [tolerance=±5% power=0.25 resistance=10k package=THT]
  R18 = Resistor [tolerance=±5% power=0.25 resistance=10k package=THT]
  Arduino_Nano_33_IoT = Arduino Nano 33 IOT

nets:
  N1: EncCLK1.RO, Arduino_Nano_33_IoT.RX
  N2: EncCLK1.RE, R3.Pin_0
  GND: EncCLK1.GND, EncDat1.GND, Port1.GND, Port2.GND, EncDat2.GND, EncCLK2.GND, R3.Pin_1, R4.Pin_0, R10.Pin_0, R11.Pin_0, R12.Pin_0, R17.Pin_1, R18.Pin_1, Arduino_Nano_33_IoT.GND, Arduino_Nano_33_IoT.D13~
  N3: EncCLK1.A, Port1.CLK-
  N4: EncCLK1.B, Port1.CLK+
  VCC: EncCLK1.VCC, EncDat1.VCC, Port1.5V, Port2.5V, EncDat2.VCC, EncCLK2.VCC, R5.Pin_1, R6.Pin_0, Adjust-High_or_Low.L1, <<.Pin_1, <<.Pin_2, >>.Pin_1, >>.Pin_2, Arduino_Nano_33_IoT.VIN
  N5: EncDat1.DE, R5.Pin_0
  N6: EncDat1.DI, Arduino_Nano_33_IoT.TX
  N7: EncDat1.A, Port1.DATA-
  N8: EncDat1.B, Port1.DATA+
  N9: Port1.H1, Arduino_Nano_33_IoT.A4
  N10: Port1.H2, Arduino_Nano_33_IoT.A5
  N11: Port1.H3, Arduino_Nano_33_IoT.A6
  N12: Port1.CTRL, R13.Pin_1
  N13: Port1.DIR, R15.Pin_1
  N14: Port1.STOP, R7.Pin_0
  N15: Port1.ADJ-L, Port2.ADJ-L, <<.Pin_3, <<.Pin_4, R10.Pin_1, Arduino_Nano_33_IoT.D9~
  N16: Port1.ADJ-R, Port2.ADJ-R, >>.Pin_3, >>.Pin_4, R11.Pin_1, Arduino_Nano_33_IoT.D2
  N17: Port1.ADJ+, R17.Pin_0, Arduino_Nano_33_IoT.A0
  N18: Port2.CLK+, EncCLK2.A
  N19: Port2.CLK-, EncCLK2.B
  N20: Port2.DATA+, EncDat2.A
  N21: Port2.DATA-, EncDat2.B
  N22: Port2.H1, Arduino_Nano_33_IoT.A3
  N23: Port2.H2, Arduino_Nano_33_IoT.A2
  N24: Port2.H3, Arduino_Nano_33_IoT.A1
  N25: Port2.CTRL, R14.Pin_0
  N26: Port2.DIR, R16.Pin_0
  N27: Port2.STOP, R8.Pin_0
  N28: Port2.ADJ+, R18.Pin_0, Arduino_Nano_33_IoT.RESET, Arduino_Nano_33_IoT.A7
  N29: EncDat2.DE, R6.Pin_1
  N30: EncDat2.DI, Arduino_Nano_33_IoT.D11/MOSI, Arduino_Nano_33_IoT.+5V
  N31: EncCLK2.RO, Arduino_Nano_33_IoT.D12~/MISO
  N32: EncCLK2.RE, R4.Pin_1
  N33: R7.Pin_1, Arduino_Nano_33_IoT.D6~
  N34: R8.Pin_1, Arduino_Nano_33_IoT.D7
  N35: Adjust-High_or_Low.COM, Arduino_Nano_33_IoT.D3~
  N36: Adjust-High_or_Low.L2, R12.Pin_1
  N37: R13.Pin_0, Arduino_Nano_33_IoT.D10~
  N38: R14.Pin_1, Arduino_Nano_33_IoT.D8
  N39: R15.Pin_0, Arduino_Nano_33_IoT.D5~
  N40: R16.Pin_1, Arduino_Nano_33_IoT.D4

notes:
  MAX485EEPA+
  L        R
  Valve. Adj.
  MEAT Valve Control Board, Rev.: -.1

custom parts:
  Arduino Nano 33 IOT: The Arduino Nano 33 IoT is the easiest and cheapest point of entry to enhance existing devices (and creating new ones) to be part of the IoT and designing pico-network applications. Whether you are looking at building a sensor network connected to your office or home router, or if you want to create a BLE device sending data to a cellphone, the Nano 33 IoT is your one-stop-solution for many of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
